# Fritzing sketch Arduino_Test_Circuit (saved by Fritzing 0.9.3b)
breadboards: 1

parts:
  Part1 = Arduino Uno (Rev3)
  R1 = Resistor [tolerance=±5% resistance=1k package="0603 [SMD]"]
  R2 = Resistor [tolerance=±5% resistance=2k package="0603 [SMD]"]
  Raspberry_Pi_1 = Raspberry Pi 3 [part_number=RPI-3-V1.2]

nets:
  GND: Part1.GND, R2.Pin_1, Raspberry_Pi_1.GND
  N1: Part1.D6_PWM, Raspberry_Pi_1.GIPO14
  N2: Part1.D7, R1.Pin_0
  N3: R1.Pin_1, R2.Pin_0, Raspberry_Pi_1.GIPO15

notes:
  USB
